// Logisim project AKSHAT_SRI_COA_EXP5_IT_A.circ as structural Verilog: 1 circuit, main circuit main
module main (
  input  A2,
  input  A1,
  input  A0,
  input  A0_2,
  input  A1_2,
  output D0,
  output Y0,
  output Y1,
  output D1,
  output Y2,
  output D2,
  output Y3,
  output Y4,
  output D3,
  output Y5,
  output Y6,
  output Y7
);

  wire not_1_out, not_2_out, not_3_out, not_4_out, not_5_out;

  not not_1 (not_1_out, A0_2);
  not not_2 (not_2_out, A0_2);
  and and_1 (D0, not_1_out, not_2_out);
  and and_2 (D1, A0_2, not_2_out);
  and and_3 (D2, A0_2, not_1_out);
  and and_4 (D3, A0_2, A0_2);
  not not_3 (not_3_out, A2);
  not not_4 (not_4_out, A1);
  not not_5 (not_5_out, A0);
  and and_5 (Y0, not_5_out, not_4_out, not_3_out);
  and and_6 (Y1, A0, not_4_out, not_3_out);
  and and_7 (Y2, not_5_out, A1, not_3_out);
  and and_8 (Y3, A0, A1, not_3_out);
  and and_9 (Y4, not_5_out, not_4_out, A2);
  and and_10 (Y5, A0, not_4_out, A2);
  and and_11 (Y6, not_5_out, A1, A2);
  and and_12 (Y7, A0, A1, A2);

  assign A1_2 = A0_2;

  // Notes on the sheet:
  //   2 TO 4 LINE SINGLE BIT DECODER
  //   IT-A
  //   AKSHAT SRIVASTAVA
  //   2300320130025
  //   Experiment-5
  //   Aim - Implement 3-8 line Decoder
  //   3-8 LINE DECODER
  //   =A'2.A'1.A'0
  //   =A'2.A1.A'0
  //   =A'2.A1.A0
  //   =A2.A'1.A'0
  //   =
  //   =A2.A'1.A0
  //   =A2.A1.A'0
  //   =A2.A1.A0
  //   =A'2.A'1.A0
endmodule
