// Logisim project AKSHAT_SRI_IT_A_COA_EXP6.circ as structural Verilog: 1 circuit, main circuit main
module main (
  input  in_1,
  input  in_2,
  input  in_3,
  input  in_4,
  input  in_5,
  input  in_6,
  output out_7
);

  wire and_1_out, and_2_out, and_3_out, and_4_out, buffer_1_out, buffer_2_out;

  buf buffer_1 (buffer_1_out, in_1);
  buf buffer_2 (buffer_2_out, in_2);
  buf and_1 (and_1_out, in_2);  // AND_Gate
  buf and_2 (and_2_out, buffer_2_out);  // AND_Gate
  buf and_3 (and_3_out, in_2);  // AND_Gate
  buf and_4 (and_4_out, buffer_2_out);  // AND_Gate
  or or_1 (out_7, and_1_out, and_2_out, and_3_out, and_4_out);

  // Notes on the sheet:
  //   2300320130025
  //   IT-A
  //   AKSHAT SRIVASTAVA
  //   4*1 MULTIPLEXER
  //   Experiment-6
  //   Aim - Design 4*1 and 8*1 Multiplexers using COA Simulator
endmodule
