// Logisim project COA LAB EXP4 (AKSHAT).circ as structural Verilog: 1 circuit, main circuit main
module main (
  input  in_1,
  input  in_2,
  input  in_3,
  input  in_4,
  input  in_5,
  input  in_6,
  input  in_7,
  input  in_8,
  output out_9,
  output out_10,
  output out_11,
  output out_12,
  output out_13,
  output out_14,
  output out_15,
  output out_16
);

  xor xor_1 (out_11, in_1, in_3);
  xor xor_2 (out_13, in_3, in_5);
  xor xor_3 (out_15, in_5, in_7);
  xor xor_4 (out_12, in_2, in_4);
  xor xor_5 (out_14, out_12, in_6);
  xor xor_6 (out_16, out_14, in_8);

  assign out_9 = in_1;
  assign out_10 = in_2;

  // Notes on the sheet:
  //   IT-A
  //   AKSHAT SRIVASTAVA
  //   2300320130025
  //   0100--------->0111
  //   LOGIC CIRCUIT FOR BINARY TO GRAY CODE CONVERTER
  //   Experiment - 4
  //   Aim: Implementing Binary-to-Gray,Gray-to-Binary code conversions using COA Simulator
  //   0110---------->0100
  //   LOGIC CIRCUIT FOR GRAY TO BINARY CODE CONVERTER
endmodule
