// Logisim project aj_1.circ as structural Verilog: 1 circuit, main circuit main
module main (
  input  _1__AND_gate,
  input  _5__NOR_gate,
  input  in_3,
  input  in_4,
  input  _2__OR_gate,
  input  _6__X_OR_gate,
  input  in_7,
  input  in_8,
  input  _7_X_NOR_gate,
  input  _3__NOT_gate,
  input  in_11,
  input  _4__NAND_gate,
  input  in_13,
  output out_14,
  output out_15,
  output out_16,
  output out_17,
  output out_18,
  output out_19,
  output out_20
);

  and and_1 (out_14, _1__AND_gate, in_3);
  or or_1 (out_16, _2__OR_gate, in_7);
  not not_1 (out_18, _3__NOT_gate);
  nand nand_1 (out_20, _4__NAND_gate, in_13);
  nor nor_1 (out_15, _5__NOR_gate, in_4);
  xor xor_1 (out_17, _6__X_OR_gate, in_8);
  xnor xnor_1 (out_19, _7_X_NOR_gate, in_11);

  // Notes on the sheet:
  //   AKSHAT SRIVASTAVA
  //   2300320130025
  //   IT-A 
  //   EXPERIMENT-1
  //   AIM:- Implement different logic gates and verify the truth table
endmodule
