// Logisim project aj_3.circ as structural Verilog: 1 circuit, main circuit main
module main (
  input  A,
  input  A_2,
  input  B,
  input  B_2,
  input  carry_in,
  output sum,
  output HS,
  output CO,
  output carry
);

  wire and_2_out, and_3_out, xor_2_out;

  xor xor_1 (HS, A_2, B);
  and and_1 (CO, A_2, B);
  xor xor_2 (xor_2_out, A, B_2);
  and and_2 (and_2_out, A, B_2);
  xor xor_3 (sum, xor_2_out, carry_in);
  and and_3 (and_3_out, xor_2_out, carry_in);
  or or_1 (carry, and_3_out, and_2_out);

  // Notes on the sheet:
  //   AKSHAT SRIVASTAVA
  //   2300320130025
  //   IT_A       Sem:- III
  //   HALF ADDER
  //   Experiment- 3
  //   Aim:- Implementing HALF ADDER, FULL ADDER  using Basic gates
  //   FULL ADDER
endmodule
