// Logisim project aj_ex_2.circ as structural Verilog: 1 circuit, main circuit main
module main (
  input  in_1,
  input  in_2,
  input  in_3,
  input  in_4,
  input  in_5,
  input  in_6,
  input  in_7,
  input  in_8,
  input  in_9,
  input  in_10,
  input  in_11,
  input  in_12,
  input  in_13,
  input  in_14,
  input  in_15,
  input  in_16,
  input  in_17,
  input  B_Using_NOR_gate,
  input  in_19,
  input  B_Using_NOR_gate_2,
  input  in_21,
  input  in_22,
  output out_23,
  output out_24,
  output out_25,
  output out_26,
  output out_27,
  output out_28,
  output out_29,
  output out_30,
  output out_31,
  output out_32,
  output out_33,
  output out_34
);

  wire nand_1_out, nand_3_out, nand_5_out, nand_6_out, nand_7_out, nand_8_out, nand_9_out, nand_10_out,
       nand_11_out, nand_13_out, nand_16_out, nand_17_out, nand_18_out, nor_1_out, nor_2_out, nor_4_out,
       nor_6_out, nor_7_out, nor_8_out, nor_9_out, nor_10_out, nor_11_out, nor_14_out, nor_16_out,
       nor_17_out, nor_18_out;

  nand nand_1 (nand_1_out, in_2, in_4);
  nor nor_1 (nor_1_out, B_Using_NOR_gate, in_21);
  nand nand_2 (out_25, nand_1_out, nand_1_out);
  nor nor_2 (nor_2_out, in_8, in_8);
  nor nor_3 (out_27, nor_2_out, nor_4_out);
  nor nor_4 (nor_4_out, in_9, in_9);
  nand nand_3 (nand_3_out, in_13, in_13);
  nand nand_4 (out_30, nand_3_out, nand_5_out);
  nand nand_5 (nand_5_out, in_15, in_15);
  nor nor_5 (out_33, nor_1_out, nor_1_out);
  nand nand_6 (nand_6_out, in_1, in_5);
  nor nor_6 (nor_6_out, in_7, in_10);
  nand nand_7 (nand_7_out, in_14, in_16);
  nor nor_7 (nor_7_out, B_Using_NOR_gate_2, in_22);
  nand nand_8 (nand_8_out, in_1, nand_6_out);
  nand nand_9 (nand_9_out, nand_6_out, in_5);
  nor nor_8 (nor_8_out, in_7, nor_6_out);
  nor nor_9 (nor_9_out, nor_6_out, in_10);
  nand nand_10 (nand_10_out, in_14, nand_7_out);
  nand nand_11 (nand_11_out, nand_7_out, in_16);
  nor nor_10 (nor_10_out, B_Using_NOR_gate_2, nor_7_out);
  nor nor_11 (nor_11_out, nor_7_out, in_22);
  nand nand_12 (out_24, nand_13_out, nand_13_out);
  nand nand_13 (nand_13_out, nand_8_out, nand_9_out);
  nor nor_12 (out_28, nor_8_out, nor_9_out);
  nand nand_14 (out_31, nand_10_out, nand_11_out);
  nor nor_13 (out_34, nor_14_out, nor_14_out);
  nor nor_14 (nor_14_out, nor_10_out, nor_11_out);
  nand nand_15 (out_23, in_3, in_3);
  nor nor_15 (out_26, in_6, in_6);
  nand nand_16 (nand_16_out, in_11, in_11);
  nand nand_17 (nand_17_out, in_12, in_12);
  nor nor_16 (nor_16_out, in_17, in_17);
  nor nor_17 (nor_17_out, in_19, in_19);
  nand nand_18 (nand_18_out, nand_16_out, nand_17_out);
  nor nor_18 (nor_18_out, nor_16_out, nor_17_out);
  nand nand_19 (out_29, nand_18_out, nand_18_out);
  nor nor_19 (out_32, nor_18_out, nor_18_out);

  // Notes on the sheet:
  //   AKSHAT SRIVASTAVA
  //   2300320130025
  //   IT-A III SEM
  //   1.AND gate using--
  //   A) using NAND gate
  //   B) using NOR gate
  //   2. OR gate using--
  //   A)Using NAND gate
  //   3.X-NOR gate using--
  //   A) using NAND gate
  //   B) using NOR gate
  //   4.X-OR gate using--
  //   A) using NAND gate
  //   EXPERIMENT- 2
  //   AIM:- Implement different logic gates using universal gates
  //   5.NOT gate using--
  //   A) using NAND gate
  //   B) using NOR gate
  //   6.NOR gate using NAND 
  //   7.NAND using NOR gate
endmodule
